# Fritzing sketch micro-bit-badge (saved by Fritzing 0.9.3b)
circuit board: 5.2cm x 7.15cm
breadboards: 1

parts:
  P12 = Pad [width=1 height=5 connect=center]  # not connected
  P11 = Pad [width=1 height=5 connect=center]
  P10 = Pad [width=1 height=5 connect=center]
  P9 = Pad [width=1 height=5 connect=center]
  P8 = Pad [width=1 height=5 connect=center]
  P7 = Pad [width=1 height=5 connect=center]
  P6 = Pad [width=1 height=5 connect=center]
  P5 = Pad [width=1 height=5 connect=center]
  P4 = Pad [width=1 height=5 connect=center]
  P3 = Pad [width=1 height=5 connect=center]
  P13_SCK = Pad [width=1 height=5 connect=center]
  P14_MISO = Pad [width=1 height=5 connect=center]
  P15_MOSI = Pad [width=1 height=5 connect=center]
  P16 = Pad [width=1 height=5 connect=center]
  3v3 = Pad [width=1 height=5 connect=center]
  3v3_2 = Pad [width=1 height=5 connect=center]
  P19 = Pad [width=1 height=5 connect=center]
  P20 = Pad [width=1 height=5 connect=center]
  GND = Pad [width=1 height=5 connect=center]
  GND_2 = Pad [width=1 height=5 connect=center]
  GND_3 = micro:bit large pad [form="♀ (female)"]
  3v3_3 = micro:bit large pad [form="♀ (female)"]
  P2 = micro:bit large pad [form="♀ (female)"]
  P1 = micro:bit large pad [form="♀ (female)"]
  P0 = micro:bit large pad [form="♀ (female)"]
  P21 = Pad [width=1 height=5 connect=center]
  P22 = Pad [width=1 height=5 connect=center]
  P23 = Pad [width=1 height=5 connect=center]
  P24 = Pad [width=1 height=5 connect=center]
  P25 = Pad [width=1 height=5 connect=center]
  P26 = Pad [width=1 height=5 connect=center]
  P27 = Pad [width=1 height=5 connect=center]
  P28 = Pad [width=1 height=5 connect=center]
  P29 = Pad [width=1 height=5 connect=center]
  P30 = Pad [width=1 height=5 connect=center]
  P31 = Pad [width=1 height=5 connect=center]  # not connected
  P32 = Pad [width=1 height=5 connect=center]
  P33 = Pad [width=1 height=5 connect=center]
  P34 = Pad [width=1 height=5 connect=center]
  3v4 = Pad [width=1 height=5 connect=center]
  3v5 = Pad [width=1 height=5 connect=center]
  P35 = Pad [width=1 height=5 connect=center]
  P36 = Pad [width=1 height=5 connect=center]
  GND1 = Pad [width=1 height=5 connect=center]
  GND2 = Pad [width=1 height=5 connect=center]
  GND3 = micro:bit large pad [form="♀ (female)"]
  3v6 = micro:bit large pad [form="♀ (female)"]
  P37 = micro:bit large pad [form="♀ (female)"]
  P38 = micro:bit large pad [form="♀ (female)"]
  P39 = micro:bit large pad [form="♀ (female)"]
  Pin_header = double row female pin header, 20 pins [form="♀ (female)"]
  Battery = FKIT-COIN_CELL [package=fkit-lir2450-h]
  P54 = Pad [width=1 height=5 connect=center]
  GND5 = Pad [width=1 height=5 connect=center]
  GND4 = Pad [width=1 height=5 connect=center]
  P55 = Pad [width=1 height=5 connect=center]
  3v8 = Pad [width=1 height=5 connect=center]
  3v7 = Pad [width=1 height=5 connect=center]
  P53 = Pad [width=1 height=5 connect=center]
  P52 = Pad [width=1 height=5 connect=center]
  P51 = Pad [width=1 height=5 connect=center]
  P50 = Pad [width=1 height=5 connect=center]  # not connected
  P49 = Pad [width=1 height=5 connect=center]
  P48 = Pad [width=1 height=5 connect=center]
  P47 = Pad [width=1 height=5 connect=center]
  P46 = Pad [width=1 height=5 connect=center]
  P45 = Pad [width=1 height=5 connect=center]
  P44 = Pad [width=1 height=5 connect=center]
  P43 = Pad [width=1 height=5 connect=center]
  P42 = Pad [width=1 height=5 connect=center]
  P41 = Pad [width=1 height=5 connect=center]
  P40 = Pad [width=1 height=5 connect=center]
  GND6 = Pad [width=4.8099999999999996 height=5 connect=center]
  3v9 = Pad [width=4.8099999999999996 height=5 connect=center]
  P56 = Pad [width=4.8099999999999996 height=5 connect=center]
  P57 = Pad [width=4.8099999999999996 height=5 connect=center]
  P58 = Pad [width=4.8099999999999996 height=5 connect=center]
  SG1 = Buzzer 12mm [package=buzzer-ccv-kit]

nets:
  N1: P11.pad, P32.pad, Pin_header.pin16, P51.pad
  N2: P10.pad, P33.pad, Pin_header.pin5, P52.pad
  N3: P9.pad, P34.pad, Pin_header.pin15, P53.pad
  N4: P8.pad, 3v4.pad, Pin_header.pin6, 3v7.pad
  N5: P7.pad, 3v5.pad, Pin_header.pin14, 3v8.pad
  N6: P6.pad, P35.pad, Pin_header.pin7, P54.pad
  N7: P5.pad, P36.pad, Pin_header.pin13, P55.pad
  N8: P4.pad, GND1.pad, Pin_header.pin8, GND4.pad
  N9: P3.pad, GND2.pad, Pin_header.pin12, GND5.pad
  N10: P13_SCK.pad, P30.pad, Pin_header.pin4, P49.pad
  N11: P14_MISO.pad, P29.pad, Pin_header.pin17, P48.pad
  N12: P15_MOSI.pad, P28.pad, Pin_header.pin3, P47.pad
  N13: P16.pad, P27.pad, Pin_header.pin18, P46.pad
  N14: 3v3.pad, 3v3_2.pad, 3v3_3.pin1, P25.pad, P26.pad, P38.pin1, Pin_header.pin1, Battery.POS, P45.pad, P44.pad, P57.pad
  N15: P19.pad, P24.pad, Pin_header.pin2, P43.pad
  N16: P20.pad, P23.pad, Pin_header.pin19, P42.pad
  N17: GND.pad, GND_2.pad, GND_3.pin1, P21.pad, P22.pad, P39.pin1, Pin_header.pin20, Battery.NEG, P41.pad, P40.pad, P58.pad, SG1.1
  N18: P2.pin1, P37.pin1, Pin_header.pin9, P56.pad
  N19: P1.pin1, 3v6.pin1, Pin_header.pin11, 3v9.pad
  N20: P0.pin1, GND3.pin1, Pin_header.pin10, GND6.pad, SG1.2

notes:
  0
  1
  2
  3
  11
  13
  14
  15
  16
  19
  20
  3v3
  GND
  5
  4
  7
  6
  9
  8
  10
  v1.0
